// Logisim project main.circ as structural Verilog: 6 circuits, main circuit engine with controls
module _32_32_buffer (
  input  [31:0] Input_row,
  input  Write_row,
  input  [4:0] Row_selector,
  output [31:0] Row_0,
  output [31:0] Row_1,
  output [31:0] Row_2,
  output [31:0] Row_3,
  output [31:0] Row_4,
  output [31:0] Row_5,
  output [31:0] Row_6,
  output [31:0] Row_7,
  output [31:0] Row_8,
  output [31:0] Row_9,
  output [31:0] Row_10,
  output [31:0] Row_11,
  output [31:0] Row_12,
  output [31:0] Row_13,
  output [31:0] Row_14,
  output [31:0] Row_15,
  output [31:0] Row_16,
  output [31:0] Row_17,
  output [31:0] Row_18,
  output [31:0] Row_19,
  output [31:0] Row_20,
  output [31:0] Row_21,
  output [31:0] Row_22,
  output [31:0] Row_23,
  output [31:0] Row_24,
  output [31:0] Row_25,
  output [31:0] Row_26,
  output [31:0] Row_27,
  output [31:0] Row_28,
  output [31:0] Row_29,
  output [31:0] Row_30,
  output [31:0] Row_31
);

  wire decoder_1_out0, decoder_1_out1, decoder_1_out2, decoder_1_out3, decoder_1_out4, decoder_1_out5,
       decoder_1_out6, decoder_1_out7, decoder_1_out8, decoder_1_out9, decoder_1_out10, decoder_1_out11,
       decoder_1_out12, decoder_1_out13, decoder_1_out14, decoder_1_out15, decoder_1_out16, decoder_1_out17,
       decoder_1_out18, decoder_1_out19, decoder_1_out20, decoder_1_out21, decoder_1_out22, decoder_1_out23,
       decoder_1_out24, decoder_1_out25, decoder_1_out26, decoder_1_out27, decoder_1_out28, decoder_1_out29,
       decoder_1_out30, decoder_1_out31;

  Decoder #(.select(5), .disabled(0)) decoder_1 (
    .out0(decoder_1_out0), .out1(decoder_1_out1), .out2(decoder_1_out2), .out3(decoder_1_out3),
    .out4(decoder_1_out4), .out5(decoder_1_out5), .out6(decoder_1_out6), .out7(decoder_1_out7),
    .out8(decoder_1_out8), .out9(decoder_1_out9), .out10(decoder_1_out10), .out11(decoder_1_out11),
    .out12(decoder_1_out12), .out13(decoder_1_out13), .out14(decoder_1_out14), .out15(decoder_1_out15),
    .out16(decoder_1_out16), .out17(decoder_1_out17), .out18(decoder_1_out18), .out19(decoder_1_out19),
    .out20(decoder_1_out20), .out21(decoder_1_out21), .out22(decoder_1_out22), .out23(decoder_1_out23),
    .out24(decoder_1_out24), .out25(decoder_1_out25), .out26(decoder_1_out26), .out27(decoder_1_out27),
    .out28(decoder_1_out28), .out29(decoder_1_out29), .out30(decoder_1_out30), .out31(decoder_1_out31),
    .sel(Row_selector), .en(Write_row));
  Register #(.width(32)) register_1 (.D(Input_row), .Q(Row_0), .clk(decoder_1_out0));  // open: en, clr
  Register #(.width(32)) register_2 (.D(Input_row), .Q(Row_1), .clk(decoder_1_out1));  // open: en, clr
  Register #(.width(32)) register_3 (.D(Input_row), .Q(Row_2), .clk(decoder_1_out2));  // open: en, clr
  Register #(.width(32)) register_4 (.D(Input_row), .Q(Row_3), .clk(decoder_1_out3));  // open: en, clr
  Register #(.width(32)) register_5 (.D(Input_row), .Q(Row_4), .clk(decoder_1_out4));  // open: en, clr
  Register #(.width(32)) register_6 (.D(Input_row), .Q(Row_5), .clk(decoder_1_out5));  // open: en, clr
  Register #(.width(32)) register_7 (.D(Input_row), .Q(Row_6), .clk(decoder_1_out6));  // open: en, clr
  Register #(.width(32)) register_8 (.D(Input_row), .Q(Row_7), .clk(decoder_1_out7));  // open: en, clr
  Register #(.width(32)) register_9 (.D(Input_row), .Q(Row_8), .clk(decoder_1_out8));  // open: en, clr
  Register #(.width(32)) register_10 (.D(Input_row), .Q(Row_9), .clk(decoder_1_out9));  // open: en, clr
  Register #(.width(32)) register_11 (.D(Input_row), .Q(Row_10), .clk(decoder_1_out10));  // open: en, clr
  Register #(.width(32)) register_12 (.D(Input_row), .Q(Row_11), .clk(decoder_1_out11));  // open: en, clr
  Register #(.width(32)) register_13 (.D(Input_row), .Q(Row_12), .clk(decoder_1_out12));  // open: en, clr
  Register #(.width(32)) register_14 (.D(Input_row), .Q(Row_13), .clk(decoder_1_out13));  // open: en, clr
  Register #(.width(32)) register_15 (.D(Input_row), .Q(Row_14), .clk(decoder_1_out14));  // open: en, clr
  Register #(.width(32)) register_16 (.D(Input_row), .Q(Row_15), .clk(decoder_1_out15));  // open: en, clr
  Register #(.width(32)) register_17 (.D(Input_row), .Q(Row_16), .clk(decoder_1_out16));  // open: en, clr
  Register #(.width(32)) register_18 (.D(Input_row), .Q(Row_17), .clk(decoder_1_out17));  // open: en, clr
  Register #(.width(32)) register_19 (.D(Input_row), .Q(Row_18), .clk(decoder_1_out18));  // open: en, clr
  Register #(.width(32)) register_20 (.D(Input_row), .Q(Row_19), .clk(decoder_1_out19));  // open: en, clr
  Register #(.width(32)) register_21 (.D(Input_row), .Q(Row_20), .clk(decoder_1_out20));  // open: en, clr
  Register #(.width(32)) register_22 (.D(Input_row), .Q(Row_21), .clk(decoder_1_out21));  // open: en, clr
  Register #(.width(32)) register_23 (.D(Input_row), .Q(Row_22), .clk(decoder_1_out22));  // open: en, clr
  Register #(.width(32)) register_24 (.D(Input_row), .Q(Row_23), .clk(decoder_1_out23));  // open: en, clr
  Register #(.width(32)) register_25 (.D(Input_row), .Q(Row_24), .clk(decoder_1_out24));  // open: en, clr
  Register #(.width(32)) register_26 (.D(Input_row), .Q(Row_25), .clk(decoder_1_out25));  // open: en, clr
  Register #(.width(32)) register_27 (.D(Input_row), .Q(Row_26), .clk(decoder_1_out26));  // open: en, clr
  Register #(.width(32)) register_28 (.D(Input_row), .Q(Row_27), .clk(decoder_1_out27));  // open: en, clr
  Register #(.width(32)) register_29 (.D(Input_row), .Q(Row_28), .clk(decoder_1_out28));  // open: en, clr
  Register #(.width(32)) register_30 (.D(Input_row), .Q(Row_29), .clk(decoder_1_out29));  // open: en, clr
  Register #(.width(32)) register_31 (.D(Input_row), .Q(Row_30), .clk(decoder_1_out30));  // open: en, clr
  Register #(.width(32)) register_32 (.D(Input_row), .Q(Row_31), .clk(decoder_1_out31));  // open: en, clr

  // Other names for the same wires on the sheet: row0[31:0] = Row_0; row1[31:0] = Row_1; row2[31:0] = Row_2;
  //   row3[31:0] = Row_3; row4[31:0] = Row_4; row5[31:0] = Row_5; row6[31:0] = Row_6; row7[31:0] = Row_7;
  //   row8[31:0] = Row_8; row9[31:0] = Row_9; row10[31:0] = Row_10; row11[31:0] = Row_11; row12[31:0] = Row_12;
  //   row13[31:0] = Row_13; row14[31:0] = Row_14; row15[31:0] = Row_15; row16[31:0] = Row_16; row17[31:0] = Row_17;
  //   row18[31:0] = Row_18; row19[31:0] = Row_19; row20[31:0] = Row_20; row21[31:0] = Row_21; row22[31:0] = Row_22;
  //   row23[31:0] = Row_23; row24[31:0] = Row_24; row25[31:0] = Row_25; row26[31:0] = Row_26; row27[31:0] = Row_27;
  //   row28[31:0] = Row_28; row29[31:0] = Row_29; row30[31:0] = Row_30; row31[31:0] = Row_31
endmodule

module Keyboard_controller (
  input  [6:0] ASCII_code,
  output [4:0] Y,
  output [4:0] X,
  output Switch
);

  wire _0x_y, _0x_y_t, minus_x0y, minus_x_y, minus_x_y_t, or_1_out, or_2_out, or_3_out, or_4_out, or_5_out,
       or_6_out, plus_x0y, plus_x_y, plus_x_y_t;
  wire [4:0] counter_2_q;

  Comparator #(.width(7)) comparator_1 (.a(ASCII_code), .b(7'b0110111), .eq(plus_x_y_t));  // open: gt, lt
  Comparator #(.width(7)) comparator_2 (.a(ASCII_code), .b(7'b0110100), .eq(plus_x0y));  // open: gt, lt
  Comparator #(.width(7)) comparator_3 (.a(ASCII_code), .b(7'b0110001), .eq(plus_x_y));  // open: gt, lt
  Comparator #(.width(7)) comparator_4 (.a(ASCII_code), .b(7'b0111000), .eq(_0x_y_t));  // open: gt, lt
  Comparator #(.width(7)) comparator_5 (.a(ASCII_code), .b(7'b0110101), .eq(Switch));  // open: gt, lt
  Comparator #(.width(7)) comparator_6 (.a(ASCII_code), .b(7'b0110010), .eq(_0x_y));  // open: gt, lt
  Comparator #(.width(7)) comparator_7 (.a(ASCII_code), .b(7'b0111001), .eq(minus_x_y_t));  // open: gt, lt
  Comparator #(.width(7)) comparator_8 (.a(ASCII_code), .b(7'b0110110), .eq(minus_x0y));  // open: gt, lt
  Comparator #(.width(7)) comparator_9 (.a(ASCII_code), .b(7'b0110011), .eq(minus_x_y));  // open: gt, lt
  or or_1 (or_1_out, minus_x_y_t, _0x_y_t, plus_x_y_t);
  or or_2 (or_2_out, or_1_out, or_3_out);
  or or_3 (or_3_out, minus_x_y, _0x_y, plus_x_y);
  or or_4 (or_4_out, minus_x_y_t, minus_x0y, minus_x_y);
  or or_5 (or_5_out, or_4_out, or_6_out);
  or or_6 (or_6_out, plus_x_y_t, plus_x0y, plus_x_y);
  // Probe on Y
  Counter #(.width(5), .max('h1f)) counter_1 (
    .load(or_1_out), .count(or_2_out), .Q(Y), .clk(or_2_out));  // open: D, carry, clr
  Counter #(.width(5), .max('h1f)) counter_2 (
    .load(or_4_out), .count(or_5_out), .Q(counter_2_q), .clk(or_5_out));  // open: D, carry, clr
  // Probe on X
  Adder #(.width(5)) adder_1 (.a({5{1'b1}}), .b(counter_2_q), .out(X));  // open: cin, cout

  // Other names for the same wires on the sheet: _0x0y = Switch

  // Notes on the sheet:
  //   Y position
  //   X position
endmodule

module SELECT (
  input  [31:0] Input1,
  input  Switch,
  input  [31:0] Input2,
  output [31:0] Output
);

  Multiplexer #(.width(32), .disabled(0), .enable("false")) multiplexer_1 (
    .in0(Input1), .in1(Input2), .out(Output), .sel(Switch));
endmodule

module bit_invertor (
  input  [31:0] INPUT9,
  input  [31:0] INPUT1,
  input  [31:0] INPUT10,
  input  [31:0] INPUT17,
  input  [31:0] INPUT2,
  input  [31:0] INPUT11,
  input  [31:0] INPUT18,
  input  [31:0] INPUT25,
  input  [31:0] INPUT3,
  input  [31:0] INPUT12,
  input  [31:0] INPUT19,
  input  [31:0] INPUT26,
  input  [31:0] INPUT4,
  input  SWITCH,
  input  [31:0] INPUT13,
  input  [31:0] INPUT20,
  input  [31:0] INPUT27,
  input  [4:0] Y,
  input  [31:0] INPUT5,
  input  [4:0] X,
  input  [31:0] INPUT14,
  input  [31:0] INPUT21,
  input  [31:0] INPUT28,
  input  [31:0] INPUT6,
  input  [31:0] INPUT15,
  input  [31:0] INPUT22,
  input  [31:0] INPUT29,
  input  [31:0] INPUT7,
  input  [31:0] INPUT16,
  input  [31:0] INPUT23,
  input  [31:0] INPUT30,
  input  [31:0] INPUT8,
  input  [31:0] INPUT24,
  input  [31:0] INPUT31,
  input  [31:0] INPUT32,
  output [31:0] CHANGED_STRING,
  output [31:0] OUTPUT1,
  output [31:0] OUTPUT2,
  output [31:0] OUTPUT3,
  output [31:0] OUTPUT4,
  output [31:0] OUTPUT5,
  output [31:0] OUTPUT6,
  output [31:0] OUTPUT7,
  output [31:0] OUTPUT8,
  output [31:0] OUTPUT9,
  output [31:0] OUTPUT10,
  output [31:0] OUTPUT11,
  output [31:0] OUTPUT12,
  output [31:0] OUTPUT13,
  output [31:0] OUTPUT14,
  output [31:0] OUTPUT15,
  output [31:0] OUTPUT16,
  output [31:0] OUTPUT17,
  output [31:0] OUTPUT18,
  output [31:0] OUTPUT19,
  output [31:0] OUTPUT20,
  output [31:0] OUTPUT21,
  output [31:0] OUTPUT22,
  output [31:0] OUTPUT23,
  output [31:0] OUTPUT24,
  output [31:0] OUTPUT25,
  output [31:0] OUTPUT26,
  output [31:0] OUTPUT27,
  output [31:0] OUTPUT28,
  output [31:0] OUTPUT29,
  output [31:0] OUTPUT30,
  output [31:0] OUTPUT31,
  output [31:0] OUTPUT32
);

  wire decoder_2_out0, decoder_2_out1, decoder_2_out2, decoder_2_out3, decoder_2_out4, decoder_2_out5,
       decoder_2_out6, decoder_2_out7, decoder_2_out8, decoder_2_out9, decoder_2_out10, decoder_2_out11,
       decoder_2_out12, decoder_2_out13, decoder_2_out14, decoder_2_out15, decoder_2_out16, decoder_2_out17,
       decoder_2_out18, decoder_2_out19, decoder_2_out20, decoder_2_out21, decoder_2_out22, decoder_2_out23,
       decoder_2_out24, decoder_2_out25, decoder_2_out26, decoder_2_out27, decoder_2_out28, decoder_2_out29,
       decoder_2_out30, decoder_2_out31;
  wire [31:0] decoder_1_out0, multiplexer_1_out, select_22_output, select_23_output, select_24_output,
       select_25_output, select_26_output, select_27_output, select_28_output, select_29_output,
       select_30_output, select_31_output, select_32_output, select_33_output, select_34_output,
       select_35_output, select_36_output, select_37_output, select_38_output, select_39_output,
       select_40_output, select_41_output, select_42_output, select_43_output, select_44_output,
       select_45_output, select_46_output, select_47_output, select_48_output, select_49_output,
       select_50_output, select_51_output, select_52_output, select_53_output, xor_1_out;

  SELECT select_1 (.Input1(INPUT1), .Switch(SWITCH), .Input2(select_22_output), .Output(OUTPUT1));
  SELECT select_2 (.Input1(INPUT2), .Switch(SWITCH), .Input2(select_23_output), .Output(OUTPUT2));
  SELECT select_3 (.Input1(INPUT3), .Switch(SWITCH), .Input2(select_24_output), .Output(OUTPUT3));
  SELECT select_4 (.Input1(INPUT4), .Switch(SWITCH), .Input2(select_25_output), .Output(OUTPUT4));
  SELECT select_5 (.Input1(INPUT5), .Switch(SWITCH), .Input2(select_26_output), .Output(OUTPUT5));
  SELECT select_6 (.Input1(INPUT6), .Switch(SWITCH), .Input2(select_27_output), .Output(OUTPUT6));
  SELECT select_7 (.Input1(INPUT7), .Switch(SWITCH), .Input2(select_28_output), .Output(OUTPUT7));
  SELECT select_8 (.Input1(INPUT8), .Switch(SWITCH), .Input2(select_29_output), .Output(OUTPUT8));
  SELECT select_9 (.Input1(INPUT9), .Switch(SWITCH), .Input2(select_30_output), .Output(OUTPUT9));
  SELECT select_10 (.Input1(INPUT10), .Switch(SWITCH), .Input2(select_31_output), .Output(OUTPUT10));
  SELECT select_11 (.Input1(INPUT11), .Switch(SWITCH), .Input2(select_32_output), .Output(OUTPUT11));
  Multiplexer #(.select(5), .width(32), .enable("false")) multiplexer_1 (
    .in0(INPUT1), .in1(INPUT2), .in2(INPUT3), .in3(INPUT4), .in4(INPUT5), .in5(INPUT6), .in6(INPUT7),
    .in7(INPUT8), .in8(INPUT9), .in9(INPUT10), .in10(INPUT11), .in11(INPUT12), .in12(INPUT13),
    .in13(INPUT14), .in14(INPUT15), .in15(INPUT16), .in16(INPUT17), .in17(INPUT18), .in18(INPUT19),
    .in19(INPUT20), .in20(INPUT21), .in21(INPUT22), .in22(INPUT23), .in23(INPUT24), .in24(INPUT25),
    .in25(INPUT26), .in26(INPUT27), .in27(INPUT28), .in28(INPUT29), .in29(INPUT30), .in30(INPUT31),
    .in31(INPUT32), .out(multiplexer_1_out), .sel(Y));
  SELECT select_12 (.Input1(INPUT12), .Switch(SWITCH), .Input2(select_33_output), .Output(OUTPUT12));
  Decoder #(.select(5), .disabled(0)) decoder_1 (
    .out0(decoder_1_out0[0]), .out1(decoder_1_out0[1]), .out2(decoder_1_out0[2]), .out3(decoder_1_out0[3]),
    .out4(decoder_1_out0[4]), .out5(decoder_1_out0[5]), .out6(decoder_1_out0[6]), .out7(decoder_1_out0[7]),
    .out8(decoder_1_out0[8]), .out9(decoder_1_out0[9]), .out10(decoder_1_out0[10]),
    .out11(decoder_1_out0[11]), .out12(decoder_1_out0[12]), .out13(decoder_1_out0[13]),
    .out14(decoder_1_out0[14]), .out15(decoder_1_out0[15]), .out16(decoder_1_out0[16]),
    .out17(decoder_1_out0[17]), .out18(decoder_1_out0[18]), .out19(decoder_1_out0[19]),
    .out20(decoder_1_out0[20]), .out21(decoder_1_out0[21]), .out22(decoder_1_out0[22]),
    .out23(decoder_1_out0[23]), .out24(decoder_1_out0[24]), .out25(decoder_1_out0[25]),
    .out26(decoder_1_out0[26]), .out27(decoder_1_out0[27]), .out28(decoder_1_out0[28]),
    .out29(decoder_1_out0[29]), .out30(decoder_1_out0[30]), .out31(decoder_1_out0[31]), .sel(X), .en(SWITCH));
  Decoder #(.select(5), .disabled(0)) decoder_2 (
    .out0(decoder_2_out0), .out1(decoder_2_out1), .out2(decoder_2_out2), .out3(decoder_2_out3),
    .out4(decoder_2_out4), .out5(decoder_2_out5), .out6(decoder_2_out6), .out7(decoder_2_out7),
    .out8(decoder_2_out8), .out9(decoder_2_out9), .out10(decoder_2_out10), .out11(decoder_2_out11),
    .out12(decoder_2_out12), .out13(decoder_2_out13), .out14(decoder_2_out14), .out15(decoder_2_out15),
    .out16(decoder_2_out16), .out17(decoder_2_out17), .out18(decoder_2_out18), .out19(decoder_2_out19),
    .out20(decoder_2_out20), .out21(decoder_2_out21), .out22(decoder_2_out22), .out23(decoder_2_out23),
    .out24(decoder_2_out24), .out25(decoder_2_out25), .out26(decoder_2_out26), .out27(decoder_2_out27),
    .out28(decoder_2_out28), .out29(decoder_2_out29), .out30(decoder_2_out30), .out31(decoder_2_out31),
    .sel(Y), .en(SWITCH));
  SELECT select_13 (.Input1(INPUT13), .Switch(SWITCH), .Input2(select_34_output), .Output(OUTPUT13));
  SELECT select_14 (.Input1(INPUT14), .Switch(SWITCH), .Input2(select_35_output), .Output(OUTPUT14));
  assign xor_1_out = multiplexer_1_out ^ decoder_1_out0;  // XOR_Gate xor_1, 32 bits wide
  SELECT select_15 (.Input1(INPUT15), .Switch(SWITCH), .Input2(select_36_output), .Output(OUTPUT15));
  SELECT select_16 (.Input1(INPUT16), .Switch(SWITCH), .Input2(select_37_output), .Output(OUTPUT16));
  SELECT select_17 (.Input1(INPUT17), .Switch(SWITCH), .Input2(select_38_output), .Output(OUTPUT17));
  SELECT select_18 (.Input1(multiplexer_1_out), .Switch(SWITCH), .Input2(xor_1_out), .Output(CHANGED_STRING));
  SELECT select_19 (.Input1(INPUT18), .Switch(SWITCH), .Input2(select_39_output), .Output(OUTPUT18));
  SELECT select_20 (.Input1(INPUT19), .Switch(SWITCH), .Input2(select_40_output), .Output(OUTPUT19));
  SELECT select_21 (.Input1(INPUT20), .Switch(SWITCH), .Input2(select_41_output), .Output(OUTPUT20));
  SELECT select_22 (.Input1(INPUT1), .Switch(decoder_2_out0), .Input2(xor_1_out), .Output(select_22_output));
  SELECT select_23 (.Input1(INPUT2), .Switch(decoder_2_out1), .Input2(xor_1_out), .Output(select_23_output));
  SELECT select_24 (.Input1(INPUT3), .Switch(decoder_2_out2), .Input2(xor_1_out), .Output(select_24_output));
  SELECT select_25 (.Input1(INPUT4), .Switch(decoder_2_out3), .Input2(xor_1_out), .Output(select_25_output));
  SELECT select_26 (.Input1(INPUT5), .Switch(decoder_2_out4), .Input2(xor_1_out), .Output(select_26_output));
  SELECT select_27 (.Input1(INPUT6), .Switch(decoder_2_out5), .Input2(xor_1_out), .Output(select_27_output));
  SELECT select_28 (.Input1(INPUT7), .Switch(decoder_2_out6), .Input2(xor_1_out), .Output(select_28_output));
  SELECT select_29 (.Input1(INPUT8), .Switch(decoder_2_out7), .Input2(xor_1_out), .Output(select_29_output));
  SELECT select_30 (.Input1(INPUT9), .Switch(decoder_2_out8), .Input2(xor_1_out), .Output(select_30_output));
  SELECT select_31 (.Input1(INPUT10), .Switch(decoder_2_out9), .Input2(xor_1_out), .Output(select_31_output));
  SELECT select_32 (.Input1(INPUT11), .Switch(decoder_2_out10), .Input2(xor_1_out), .Output(select_32_output));
  SELECT select_33 (.Input1(INPUT12), .Switch(decoder_2_out11), .Input2(xor_1_out), .Output(select_33_output));
  SELECT select_34 (.Input1(INPUT13), .Switch(decoder_2_out12), .Input2(xor_1_out), .Output(select_34_output));
  SELECT select_35 (.Input1(INPUT14), .Switch(decoder_2_out13), .Input2(xor_1_out), .Output(select_35_output));
  SELECT select_36 (.Input1(INPUT15), .Switch(decoder_2_out14), .Input2(xor_1_out), .Output(select_36_output));
  SELECT select_37 (.Input1(INPUT16), .Switch(decoder_2_out15), .Input2(xor_1_out), .Output(select_37_output));
  SELECT select_38 (.Input1(INPUT17), .Switch(decoder_2_out16), .Input2(xor_1_out), .Output(select_38_output));
  SELECT select_39 (.Input1(INPUT18), .Switch(decoder_2_out17), .Input2(xor_1_out), .Output(select_39_output));
  SELECT select_40 (.Input1(INPUT19), .Switch(decoder_2_out18), .Input2(xor_1_out), .Output(select_40_output));
  SELECT select_41 (.Input1(INPUT20), .Switch(decoder_2_out19), .Input2(xor_1_out), .Output(select_41_output));
  SELECT select_42 (.Input1(INPUT21), .Switch(decoder_2_out20), .Input2(xor_1_out), .Output(select_42_output));
  SELECT select_43 (.Input1(INPUT22), .Switch(decoder_2_out21), .Input2(xor_1_out), .Output(select_43_output));
  SELECT select_44 (.Input1(INPUT23), .Switch(decoder_2_out22), .Input2(xor_1_out), .Output(select_44_output));
  SELECT select_45 (.Input1(INPUT24), .Switch(decoder_2_out23), .Input2(xor_1_out), .Output(select_45_output));
  SELECT select_46 (.Input1(INPUT25), .Switch(decoder_2_out24), .Input2(xor_1_out), .Output(select_46_output));
  SELECT select_47 (.Input1(INPUT26), .Switch(decoder_2_out25), .Input2(xor_1_out), .Output(select_47_output));
  SELECT select_48 (.Input1(INPUT27), .Switch(decoder_2_out26), .Input2(xor_1_out), .Output(select_48_output));
  SELECT select_49 (.Input1(INPUT28), .Switch(decoder_2_out27), .Input2(xor_1_out), .Output(select_49_output));
  SELECT select_50 (.Input1(INPUT29), .Switch(decoder_2_out28), .Input2(xor_1_out), .Output(select_50_output));
  SELECT select_51 (.Input1(INPUT30), .Switch(decoder_2_out29), .Input2(xor_1_out), .Output(select_51_output));
  SELECT select_52 (.Input1(INPUT31), .Switch(decoder_2_out30), .Input2(xor_1_out), .Output(select_52_output));
  SELECT select_53 (.Input1(INPUT32), .Switch(decoder_2_out31), .Input2(xor_1_out), .Output(select_53_output));
  SELECT select_54 (.Input1(INPUT21), .Switch(SWITCH), .Input2(select_42_output), .Output(OUTPUT21));
  SELECT select_55 (.Input1(INPUT22), .Switch(SWITCH), .Input2(select_43_output), .Output(OUTPUT22));
  SELECT select_56 (.Input1(INPUT23), .Switch(SWITCH), .Input2(select_44_output), .Output(OUTPUT23));
  SELECT select_57 (.Input1(INPUT24), .Switch(SWITCH), .Input2(select_45_output), .Output(OUTPUT24));
  SELECT select_58 (.Input1(INPUT25), .Switch(SWITCH), .Input2(select_46_output), .Output(OUTPUT25));
  SELECT select_59 (.Input1(INPUT26), .Switch(SWITCH), .Input2(select_47_output), .Output(OUTPUT26));
  SELECT select_60 (.Input1(INPUT27), .Switch(SWITCH), .Input2(select_48_output), .Output(OUTPUT27));
  SELECT select_61 (.Input1(INPUT28), .Switch(SWITCH), .Input2(select_49_output), .Output(OUTPUT28));
  SELECT select_62 (.Input1(INPUT29), .Switch(SWITCH), .Input2(select_50_output), .Output(OUTPUT29));
  SELECT select_63 (.Input1(INPUT30), .Switch(SWITCH), .Input2(select_51_output), .Output(OUTPUT30));
  SELECT select_64 (.Input1(INPUT31), .Switch(SWITCH), .Input2(select_52_output), .Output(OUTPUT31));
  SELECT select_65 (.Input1(INPUT32), .Switch(SWITCH), .Input2(select_53_output), .Output(OUTPUT32));
endmodule

module engine_with_controls (
  input  [7:0] birth_input,
  input  [7:0] survival_input
);

  wire and_3_out, and_4_out, and_5_out, and_6_out, and_7_out, and_8_out, and_9_out, and_10_out, and_11_out,
       and_12_out, and_13_out, and_14_out, and_15_out, and_16_out, and_17_out, and_20_out, and_21_out,
       and_22_out, and_23_out, and_24_out, and_25_out, and_26_out, and_27_out, and_28_out, and_29_out,
       and_30_out, and_31_out, and_32_out, and_33_out, and_34_out, cdm_8_mark5_1_p1, cdm_8_mark5_1_p2,
       cdm_8_mark5_1_p4, cdm_8_mark5_1_p5, cdm_8_mark5_1_p6, cdm_8_mark5_1_p7, cdm_8_mark5_1_p8,
       cdm_8_mark5_1_p9, cdm_8_mark5_2_p1, cdm_8_mark5_2_p2, cdm_8_mark5_2_p4, cdm_8_mark5_2_p5,
       cdm_8_mark5_2_p6, cdm_8_mark5_2_p7, cdm_8_mark5_2_p8, cdm_8_mark5_2_p9, change_bit, change_bit_slow,
       clock, code, code_1, comparator_1_lt, comparator_2_eq, comparator_3_eq, comparator_4_eq,
       comparator_5_eq, comparator_6_eq, comparator_7_eq, comparator_8_eq, comparator_9_eq, comparator_10_eq,
       comparator_11_eq, comparator_12_eq, comparator_13_eq, comparator_14_eq, comparator_15_eq,
       comparator_16_eq, comparator_17_eq, comparator_18_eq, comparator_19_eq, comparator_20_lt,
       comparator_21_eq, comparator_22_eq, comparator_23_eq, comparator_24_eq, comparator_25_eq,
       comparator_26_eq, comparator_27_eq, comparator_28_eq, comparator_29_eq, comparator_30_eq,
       comparator_31_eq, comparator_32_eq, comparator_33_eq, comparator_34_eq, comparator_35_eq,
       comparator_36_eq, comparator_37_eq, comparator_38_eq, data, data_1, decoder_3_out0, decoder_4_out1,
       decoder_5_out0, decoder_5_out1, decoder_6_out0, decoder_7_out1, decoder_8_out0, decoder_8_out1,
       decoder_9_out1, decoder_10_out1, decoder_11_out0, decoder_11_out1, decoder_12_out1, decoder_13_out0,
       decoder_14_out0, decoder_14_out1, decoder_15_out1, decoder_16_out1, decoder_19_out0, decoder_20_out1,
       decoder_21_out0, decoder_21_out1, decoder_22_out0, decoder_23_out1, decoder_24_out0, decoder_24_out1,
       decoder_25_out1, decoder_26_out1, decoder_27_out0, decoder_27_out1, decoder_28_out1, decoder_29_out0,
       decoder_30_out0, decoder_30_out1, decoder_31_out1, decoder_32_out1, in_out, in_out_1, IOsel, IOsel_1,
       is_null_byte, is_null_byte_1, is_row_null, is_row_null_1, mem, mem_1, multiplexer_2_out, not_1_out,
       not_2_out, not_3_out, not_6_out, not_7_out, not_8_out, not_9_out, not_11_out, not_13_out, not_15_out,
       not_16_out, not_17_out, not_18_out, not_19_out, not_20_out, not_21_out, not_22_out, not_23_out,
       not_24_out, not_25_out, not_26_out, not_27_out, not_28_out, not_29_out, not_30_out, not_31_out,
       not_32_out, not_33_out, not_34_out, not_35_out, not_36_out, not_38_out, not_39_out, not_41_out,
       not_42_out, not_43_out, not_44_out, not_45_out, not_46_out, not_47_out, not_48_out, not_49_out,
       not_50_out, not_51_out, not_52_out, not_53_out, not_54_out, not_55_out, not_56_out, or_1_out,
       or_2_out, or_3_out, or_4_out, or_5_out, or_6_out, or_7_out, or_8_out, RAM, RAM_1, recieve_row,
       recieve_row_slow, selected_bit, selected_bit_1, send_row, send_row_slow, setting, Start_out,
       xnor_1_out, xnor_2_out, xnor_3_out;
  wire [4:0] cpuX, cpuX_1, cpuY, cpuY_1, keyboard_controller_1_x, keyboard_controller_1_y, multiplexer_3_out,
       multiplexer_4_out;
  wire [6:0] keyboard_1_data;
  wire [7:0] bus, bus_1, cdm_8_mark5_1_p13, cdm_8_mark5_1_p14, cdm_8_mark5_2_p13, cdm_8_mark5_2_p14,
       controlled_buffer_4_out, controlled_buffer_6_out, controlled_buffer_8_out, controlled_buffer_12_out,
       controlled_buffer_18_out, controlled_buffer_22_out, controlled_buffer_32_out,
       controlled_buffer_34_out, controlled_buffer_36_out, controlled_buffer_40_out,
       controlled_buffer_46_out, controlled_buffer_50_out, env_sum, env_sum_1, IO_birth_conditions,
       IO_death_conditions, IO_game_mode, IOaddr, IOaddr_1, not_4_out, register_5_q, register_7_q,
       register_9_q, register_10_q, register_11_q, register_13_q, register_15_q, register_16_q,
       register_17_q, register_18_q;
  wire [7:5] register_4_q, register_6_q, register_12_q, register_14_q;
  wire [31:0] bit_invertor_1_changed_string, bit_invertor_1_output1, bit_invertor_1_output2,
       bit_invertor_1_output3, bit_invertor_1_output4, bit_invertor_1_output5, bit_invertor_1_output6,
       bit_invertor_1_output7, bit_invertor_1_output8, bit_invertor_1_output9, bit_invertor_1_output10,
       bit_invertor_1_output11, bit_invertor_1_output12, bit_invertor_1_output13, bit_invertor_1_output14,
       bit_invertor_1_output15, bit_invertor_1_output16, bit_invertor_1_output17, bit_invertor_1_output18,
       bit_invertor_1_output19, bit_invertor_1_output20, bit_invertor_1_output21, bit_invertor_1_output22,
       bit_invertor_1_output23, bit_invertor_1_output24, bit_invertor_1_output25, bit_invertor_1_output26,
       bit_invertor_1_output27, bit_invertor_1_output28, bit_invertor_1_output29, bit_invertor_1_output30,
       bit_invertor_1_output31, bit_invertor_1_output32, cpuRow, inverted_row, multiplexer_1_out,
       n32_32_buffer_1_row_0, n32_32_buffer_1_row_1, n32_32_buffer_1_row_2, n32_32_buffer_1_row_3,
       n32_32_buffer_1_row_4, n32_32_buffer_1_row_5, n32_32_buffer_1_row_6, n32_32_buffer_1_row_7,
       n32_32_buffer_1_row_8, n32_32_buffer_1_row_9, n32_32_buffer_1_row_10, n32_32_buffer_1_row_11,
       n32_32_buffer_1_row_12, n32_32_buffer_1_row_13, n32_32_buffer_1_row_14, n32_32_buffer_1_row_15,
       n32_32_buffer_1_row_16, n32_32_buffer_1_row_17, n32_32_buffer_1_row_18, n32_32_buffer_1_row_19,
       n32_32_buffer_1_row_20, n32_32_buffer_1_row_21, n32_32_buffer_1_row_22, n32_32_buffer_1_row_23,
       n32_32_buffer_1_row_24, n32_32_buffer_1_row_25, n32_32_buffer_1_row_26, n32_32_buffer_1_row_27,
       n32_32_buffer_1_row_28, n32_32_buffer_1_row_29, n32_32_buffer_1_row_30, n32_32_buffer_1_row_31;

  Keyboard keyboard_1 (.clk(clock), .re(setting), .data(keyboard_1_data));  // open: clr, avail
  Button Start (.out(Start_out));
  not not_1 (not_1_out, Start_out);
  xnor xnor_1 (xnor_1_out, not_1_out, Start_out);
  not not_2 (not_2_out, setting);
  not not_3 (not_3_out, setting);
  Register register_1 (.D(8'h1), .Q(IO_game_mode), .clk(xnor_1_out));  // open: en, clr
  xnor xnor_2 (xnor_2_out, not_2_out, setting);
  assign not_4_out = ~survival_input;  // NOT_Gate not_4, 8 bits wide
  xnor xnor_3 (xnor_3_out, not_3_out, setting);
  not not_5 (setting, IO_game_mode[0]);
  Register register_2 (.D(birth_input), .Q(IO_birth_conditions), .clk(xnor_2_out));  // open: en, clr
  Register register_3 (.D(not_4_out), .Q(IO_death_conditions), .clk(xnor_3_out));  // open: en, clr
  // Probe on cdm_8_mark5_1_p5
  // Probe on cdm_8_mark5_1_p1
  // Probe on cdm_8_mark5_1_p2
  // Probe on cdm_8_mark5_1_p4
  Clock clock_1 (.out(clock));
  and and_1 (IOsel, not_9_out, clock, data);
  not not_6 (not_6_out, not_6_out);
  not not_7 (not_7_out, not_7_out);
  not not_8 (not_8_out, not_8_out);
  // Probe on cdm_8_mark5_1_p6
  // Probe on cdm_8_mark5_1_p7
  // Probe on cdm_8_mark5_1_p8
  // CdM_8_mark5 cdm_8_mark5_1: pin names not known; wires that end beside it: cdm_8_mark5_1_p1, cdm_8_mark5_1_p2, clock, cdm_8_mark5_1_p4, cdm_8_mark5_1_p5, cdm_8_mark5_1_p6, cdm_8_mark5_1_p7, cdm_8_mark5_1_p8, cdm_8_mark5_1_p9, mem, in_out, IOaddr, cdm_8_mark5_1_p13, cdm_8_mark5_1_p14
  not not_9 (not_9_out, comparator_1_lt);
  not not_10 (send_row_slow, not_11_out);
  not not_11 (not_11_out, send_row);
  not not_12 (recieve_row_slow, not_13_out);
  not not_13 (not_13_out, recieve_row);
  Keyboard_controller keyboard_controller_1 (
    .ASCII_code(keyboard_1_data), .X(keyboard_controller_1_x), .Y(keyboard_controller_1_y),
    .Switch(change_bit));
  not not_14 (change_bit_slow, not_15_out);
  not not_15 (not_15_out, change_bit);
  Decoder #(.disabled(0)) decoder_1 (.out0(code), .out1(data), .sel(cdm_8_mark5_1_p9), .en(mem));
  assign bus = not_16_out ? cdm_8_mark5_1_p13 : 8'bz;  // Controlled_Buffer controlled_buffer_1
  not not_16 (not_16_out, in_out);
  assign cdm_8_mark5_1_p14 = in_out ? bus : 8'bz;  // Controlled_Buffer controlled_buffer_2
  and and_2 (RAM, comparator_1_lt, data);
  // Probe on keyboard_controller_1_y
  // Probe on keyboard_controller_1_x
  assign bus = recieve_row ? {8{1'b0}} : 8'bz;  // Controlled_Buffer controlled_buffer_3
  assign controlled_buffer_4_out = decoder_3_out0 ? bus : 8'bz;  // Controlled_Buffer controlled_buffer_4
  Register register_4 (.D(controlled_buffer_4_out), .Q({register_4_q, cpuY}), .clk(not_17_out));  // open: en, clr
  not not_17 (not_17_out, not_18_out);
  Multiplexer #(.width(32), .disabled(0), .enable("false")) multiplexer_1 (
    .in0(inverted_row), .in1(cpuRow), .out(multiplexer_1_out), .sel(IO_game_mode[0]));
  Multiplexer #(.disabled(0), .enable("false")) multiplexer_2 (
    .in0(change_bit), .in1(send_row_slow), .out(multiplexer_2_out), .sel(IO_game_mode[0]));
  Multiplexer #(.width(5), .disabled(0), .enable("false")) multiplexer_3 (
    .in0(cpuY), .in1(keyboard_controller_1_y), .out(multiplexer_3_out), .sel(setting));
  Multiplexer #(.width(5), .disabled(0), .enable("false")) multiplexer_4 (
    .in0(keyboard_controller_1_x), .in1(cpuX), .out(multiplexer_4_out), .sel(IO_game_mode[0]));
  // Probe on IOaddr
  Comparator #(.mode("unsigned")) comparator_1 (.a(IOaddr), .b(8'hf0), .lt(comparator_1_lt));  // open: gt, eq
  Decoder #(.disabled(0)) decoder_2 (.out0(send_row), .out1(recieve_row), .sel(in_out), .en(and_3_out));
  Decoder #(.disabled(0)) decoder_3 (.out0(decoder_3_out0), .sel(in_out), .en(and_4_out));  // open: out1
  not not_18 (not_18_out, decoder_3_out0);
  Decoder #(.disabled(0)) decoder_4 (.out1(decoder_4_out1), .sel(in_out), .en(and_5_out));  // open: out0
  assign bus = decoder_4_out1 ? IO_game_mode : 8'bz;  // Controlled_Buffer controlled_buffer_5
  _32_32_buffer u_32_32_buffer_1 (
    .Row_0(n32_32_buffer_1_row_0), .Row_1(n32_32_buffer_1_row_1), .Row_2(n32_32_buffer_1_row_2),
    .Row_3(n32_32_buffer_1_row_3), .Row_4(n32_32_buffer_1_row_4), .Row_5(n32_32_buffer_1_row_5),
    .Row_6(n32_32_buffer_1_row_6), .Row_7(n32_32_buffer_1_row_7), .Row_8(n32_32_buffer_1_row_8),
    .Row_9(n32_32_buffer_1_row_9), .Row_10(n32_32_buffer_1_row_10), .Row_11(n32_32_buffer_1_row_11),
    .Row_12(n32_32_buffer_1_row_12), .Row_13(n32_32_buffer_1_row_13), .Row_14(n32_32_buffer_1_row_14),
    .Row_15(n32_32_buffer_1_row_15), .Row_16(n32_32_buffer_1_row_16), .Row_17(n32_32_buffer_1_row_17),
    .Row_18(n32_32_buffer_1_row_18), .Row_19(n32_32_buffer_1_row_19), .Row_20(n32_32_buffer_1_row_20),
    .Row_21(n32_32_buffer_1_row_21), .Row_22(n32_32_buffer_1_row_22), .Row_23(n32_32_buffer_1_row_23),
    .Row_24(n32_32_buffer_1_row_24), .Row_25(n32_32_buffer_1_row_25), .Row_26(n32_32_buffer_1_row_26),
    .Row_27(n32_32_buffer_1_row_27), .Row_28(n32_32_buffer_1_row_28), .Row_29(n32_32_buffer_1_row_29),
    .Row_30(n32_32_buffer_1_row_30), .Row_31(n32_32_buffer_1_row_31), .Row_selector(multiplexer_3_out),
    .Write_row(multiplexer_2_out), .Input_row(multiplexer_1_out));
  // Probe on multiplexer_3_out
  // Probe on multiplexer_4_out
  Comparator comparator_2 (.a(IOaddr), .b(8'hf5), .eq(comparator_2_eq));  // open: gt, lt
  and and_3 (and_3_out, comparator_2_eq, IOsel);
  Comparator comparator_3 (.a(IOaddr), .b(8'hf3), .eq(comparator_3_eq));  // open: gt, lt
  and and_4 (and_4_out, comparator_3_eq, IOsel);
  Comparator comparator_4 (.a(IOaddr), .b(8'hf0), .eq(comparator_4_eq));  // open: gt, lt
  and and_5 (and_5_out, comparator_4_eq, IOsel);
  // Probe on bus
  ROM rom_1 (.addr(IOaddr), .data(bus), .sel(code));
  RAM u_ram_1 (.addr(IOaddr), .data(bus), .sel(RAM), .clk(clock), .ld(in_out));  // open: clr
  env_constructor env_constructor_1 (
    .Row_0(n32_32_buffer_1_row_0), .Row_1(n32_32_buffer_1_row_1), .Row_2(n32_32_buffer_1_row_2),
    .Row_3(n32_32_buffer_1_row_3), .Row_4(n32_32_buffer_1_row_4), .Row_5(n32_32_buffer_1_row_5),
    .Row_6(n32_32_buffer_1_row_6), .Row_7(n32_32_buffer_1_row_7), .Row_8(n32_32_buffer_1_row_8),
    .Row_9(n32_32_buffer_1_row_9), .Row_10(n32_32_buffer_1_row_10), .Row_11(n32_32_buffer_1_row_11),
    .Row_12(n32_32_buffer_1_row_12), .Row_13(n32_32_buffer_1_row_13), .Row_14(n32_32_buffer_1_row_14),
    .Row_15(n32_32_buffer_1_row_15), .Row_16(n32_32_buffer_1_row_16), .Row_17(n32_32_buffer_1_row_17),
    .Row_18(n32_32_buffer_1_row_18), .Row_19(n32_32_buffer_1_row_19), .Row_20(n32_32_buffer_1_row_20),
    .Row_21(n32_32_buffer_1_row_21), .Row_22(n32_32_buffer_1_row_22), .Row_23(n32_32_buffer_1_row_23),
    .Row_24(n32_32_buffer_1_row_24), .Row_25(n32_32_buffer_1_row_25), .Row_26(n32_32_buffer_1_row_26),
    .Row_27(n32_32_buffer_1_row_27), .Row_28(n32_32_buffer_1_row_28), .Row_29(n32_32_buffer_1_row_29),
    .Row_30(n32_32_buffer_1_row_30), .Row_31(n32_32_buffer_1_row_31), .Is_row_env__null(is_row_null),
    .Is_byte_env__null(is_null_byte), .Sum(env_sum), .Bit(selected_bit), .Y__row_index(cpuY),
    .X__bit_index(cpuX));
  not not_19 (not_19_out, not_19_out);
  not not_20 (not_20_out, not_20_out);
  LED led_1 (.in(selected_bit));
  // Probe on env_sum
  assign controlled_buffer_6_out = decoder_5_out0 ? bus : 8'bz;  // Controlled_Buffer controlled_buffer_6
  assign controlled_buffer_6_out = recieve_row ? cpuRow[7:0] : 8'bz;  // Controlled_Buffer controlled_buffer_7
  assign controlled_buffer_8_out = decoder_6_out0 ? bus : 8'bz;  // Controlled_Buffer controlled_buffer_8
  assign bus = decoder_5_out1 ? register_5_q : 8'bz;  // Controlled_Buffer controlled_buffer_9
  Register register_5 (.D(controlled_buffer_6_out), .Q(register_5_q), .clk(or_1_out));  // open: en, clr
  or or_1 (or_1_out, recieve_row_slow, decoder_5_out0);
  Register register_6 (.D(controlled_buffer_8_out), .Q({register_6_q, cpuX}), .clk(not_22_out));  // open: en, clr
  not not_21 (not_21_out, decoder_6_out0);
  not not_22 (not_22_out, not_21_out);
  assign bus = decoder_7_out1 ? IO_birth_conditions : 8'bz;  // Controlled_Buffer controlled_buffer_10
  Decoder #(.disabled(0)) decoder_5 (.out0(decoder_5_out0), .out1(decoder_5_out1), .sel(in_out), .en(and_6_out));
  assign cpuRow[7:0] = send_row ? register_5_q : 8'bz;  // Controlled_Buffer controlled_buffer_11
  Decoder #(.disabled(0)) decoder_6 (.out0(decoder_6_out0), .sel(in_out), .en(and_7_out));  // open: out1
  Decoder #(.disabled(0)) decoder_7 (.out1(decoder_7_out1), .sel(in_out), .en(and_8_out));  // open: out0
  env_constructor env_constructor_2 (
    .Row_0(n32_32_buffer_1_row_0), .Row_1(n32_32_buffer_1_row_1), .Row_2(n32_32_buffer_1_row_2),
    .Row_3(n32_32_buffer_1_row_3), .Row_4(n32_32_buffer_1_row_4), .Row_5(n32_32_buffer_1_row_5),
    .Row_6(n32_32_buffer_1_row_6), .Row_7(n32_32_buffer_1_row_7), .Row_8(n32_32_buffer_1_row_8),
    .Row_9(n32_32_buffer_1_row_9), .Row_10(n32_32_buffer_1_row_10), .Row_11(n32_32_buffer_1_row_11),
    .Row_12(n32_32_buffer_1_row_12), .Row_13(n32_32_buffer_1_row_13), .Row_14(n32_32_buffer_1_row_14),
    .Row_15(n32_32_buffer_1_row_15), .Row_16(n32_32_buffer_1_row_16), .Row_17(n32_32_buffer_1_row_17),
    .Row_18(n32_32_buffer_1_row_18), .Row_19(n32_32_buffer_1_row_19), .Row_20(n32_32_buffer_1_row_20),
    .Row_21(n32_32_buffer_1_row_21), .Row_22(n32_32_buffer_1_row_22), .Row_23(n32_32_buffer_1_row_23),
    .Row_24(n32_32_buffer_1_row_24), .Row_25(n32_32_buffer_1_row_25), .Row_26(n32_32_buffer_1_row_26),
    .Row_27(n32_32_buffer_1_row_27), .Row_28(n32_32_buffer_1_row_28), .Row_29(n32_32_buffer_1_row_29),
    .Row_30(n32_32_buffer_1_row_30), .Row_31(n32_32_buffer_1_row_31), .Is_row_env__null(is_row_null_1),
    .Is_byte_env__null(is_null_byte_1), .Sum(env_sum_1), .Bit(selected_bit_1), .Y__row_index(cpuY_1),
    .X__bit_index(cpuX_1));
  Comparator comparator_5 (.a(IOaddr), .b(8'hf6), .eq(comparator_5_eq));  // open: gt, lt
  and and_6 (and_6_out, comparator_5_eq, IOsel);
  Comparator comparator_6 (.a(IOaddr), .b(8'hf4), .eq(comparator_6_eq));  // open: gt, lt
  and and_7 (and_7_out, comparator_6_eq, IOsel);
  Comparator comparator_7 (.a(IOaddr), .b(8'hf1), .eq(comparator_7_eq));  // open: gt, lt
  and and_8 (and_8_out, comparator_7_eq, IOsel);
  not not_23 (not_23_out, not_23_out);
  not not_24 (not_24_out, not_24_out);
  LED led_2 (.in(selected_bit_1));
  // Probe on env_sum_1
  assign controlled_buffer_12_out = decoder_8_out0 ? bus : 8'bz;  // Controlled_Buffer controlled_buffer_12
  assign controlled_buffer_12_out = recieve_row ? cpuRow[15:8] : 8'bz;  // Controlled_Buffer controlled_buffer_13
  or or_2 (or_2_out, recieve_row_slow, decoder_8_out0);
  assign bus = decoder_8_out1 ? register_7_q : 8'bz;  // Controlled_Buffer controlled_buffer_14
  Register register_7 (.D(controlled_buffer_12_out), .Q(register_7_q), .clk(or_2_out));  // open: en, clr
  Decoder #(.disabled(0)) decoder_8 (.out0(decoder_8_out0), .out1(decoder_8_out1), .sel(in_out), .en(and_9_out));
  assign cpuRow[15:8] = send_row ? register_7_q : 8'bz;  // Controlled_Buffer controlled_buffer_15
  Comparator comparator_8 (.a(IOaddr), .b(8'hf7), .eq(comparator_8_eq));  // open: gt, lt
  and and_9 (and_9_out, comparator_8_eq, IOsel);
  Decoder #(.disabled(0)) decoder_9 (.out1(decoder_9_out1), .sel(in_out), .en(and_10_out));  // open: out0
  assign bus = decoder_9_out1 ? {{7{1'b0}}, selected_bit} : 8'bz;  // Controlled_Buffer controlled_buffer_16
  Decoder #(.disabled(0)) decoder_10 (.out1(decoder_10_out1), .sel(in_out), .en(and_11_out));  // open: out0
  assign bus = decoder_10_out1 ? IO_death_conditions : 8'bz;  // Controlled_Buffer controlled_buffer_17
  bit_invertor bit_invertor_1 (
    .INPUT9(n32_32_buffer_1_row_8), .INPUT1(n32_32_buffer_1_row_0), .INPUT10(n32_32_buffer_1_row_9),
    .INPUT17(n32_32_buffer_1_row_16), .INPUT2(n32_32_buffer_1_row_1), .INPUT11(n32_32_buffer_1_row_10),
    .INPUT18(n32_32_buffer_1_row_17), .INPUT25(n32_32_buffer_1_row_24), .INPUT3(n32_32_buffer_1_row_2),
    .INPUT12(n32_32_buffer_1_row_11), .INPUT19(n32_32_buffer_1_row_18), .INPUT26(n32_32_buffer_1_row_25),
    .INPUT4(n32_32_buffer_1_row_3), .SWITCH(clock), .INPUT13(n32_32_buffer_1_row_12),
    .INPUT20(n32_32_buffer_1_row_19), .INPUT27(n32_32_buffer_1_row_26), .Y(multiplexer_3_out),
    .INPUT5(n32_32_buffer_1_row_4), .X(multiplexer_4_out), .INPUT14(n32_32_buffer_1_row_13),
    .INPUT21(n32_32_buffer_1_row_20), .INPUT28(n32_32_buffer_1_row_27), .INPUT6(n32_32_buffer_1_row_5),
    .INPUT15(n32_32_buffer_1_row_14), .INPUT22(n32_32_buffer_1_row_21), .INPUT29(n32_32_buffer_1_row_28),
    .INPUT7(n32_32_buffer_1_row_6), .INPUT16(n32_32_buffer_1_row_15), .INPUT23(n32_32_buffer_1_row_22),
    .INPUT30(n32_32_buffer_1_row_29), .INPUT8(n32_32_buffer_1_row_7), .INPUT24(n32_32_buffer_1_row_23),
    .INPUT31(n32_32_buffer_1_row_30), .INPUT32(n32_32_buffer_1_row_31),
    .CHANGED_STRING(bit_invertor_1_changed_string), .OUTPUT1(bit_invertor_1_output1),
    .OUTPUT2(bit_invertor_1_output2), .OUTPUT3(bit_invertor_1_output3), .OUTPUT4(bit_invertor_1_output4),
    .OUTPUT5(bit_invertor_1_output5), .OUTPUT6(bit_invertor_1_output6), .OUTPUT7(bit_invertor_1_output7),
    .OUTPUT8(bit_invertor_1_output8), .OUTPUT9(bit_invertor_1_output9), .OUTPUT10(bit_invertor_1_output10),
    .OUTPUT11(bit_invertor_1_output11), .OUTPUT12(bit_invertor_1_output12),
    .OUTPUT13(bit_invertor_1_output13), .OUTPUT14(bit_invertor_1_output14),
    .OUTPUT15(bit_invertor_1_output15), .OUTPUT16(bit_invertor_1_output16),
    .OUTPUT17(bit_invertor_1_output17), .OUTPUT18(bit_invertor_1_output18),
    .OUTPUT19(bit_invertor_1_output19), .OUTPUT20(bit_invertor_1_output20),
    .OUTPUT21(bit_invertor_1_output21), .OUTPUT22(bit_invertor_1_output22),
    .OUTPUT23(bit_invertor_1_output23), .OUTPUT24(bit_invertor_1_output24),
    .OUTPUT25(bit_invertor_1_output25), .OUTPUT26(bit_invertor_1_output26),
    .OUTPUT27(bit_invertor_1_output27), .OUTPUT28(bit_invertor_1_output28),
    .OUTPUT29(bit_invertor_1_output29), .OUTPUT30(bit_invertor_1_output30),
    .OUTPUT31(bit_invertor_1_output31), .OUTPUT32(bit_invertor_1_output32));
  not not_25 (not_25_out, clock);
  Comparator comparator_9 (.a(IOaddr), .b(8'hfa), .eq(comparator_9_eq));  // open: gt, lt
  and and_10 (and_10_out, comparator_9_eq, IOsel);
  Comparator comparator_10 (.a(IOaddr), .b(8'hf2), .eq(comparator_10_eq));  // open: gt, lt
  and and_11 (and_11_out, comparator_10_eq, IOsel);
  DotMatrix #(.inputtype("row"), .matrixcols(32), .matrixrows(32)) dotmatrix_1 (
    .row0(bit_invertor_1_output1), .row1(bit_invertor_1_output2), .row2(bit_invertor_1_output3),
    .row3(bit_invertor_1_output4), .row4(bit_invertor_1_output5), .row5(bit_invertor_1_output6),
    .row6(bit_invertor_1_output7), .row7(bit_invertor_1_output8), .row8(bit_invertor_1_output9),
    .row9(bit_invertor_1_output10), .row10(bit_invertor_1_output11), .row11(bit_invertor_1_output12),
    .row12(bit_invertor_1_output13), .row13(bit_invertor_1_output14), .row14(bit_invertor_1_output15),
    .row15(bit_invertor_1_output16), .row16(bit_invertor_1_output17), .row17(bit_invertor_1_output18),
    .row18(bit_invertor_1_output19), .row19(bit_invertor_1_output20), .row20(bit_invertor_1_output21),
    .row21(bit_invertor_1_output22), .row22(bit_invertor_1_output23), .row23(bit_invertor_1_output24),
    .row24(bit_invertor_1_output25), .row25(bit_invertor_1_output26), .row26(bit_invertor_1_output27),
    .row27(bit_invertor_1_output28), .row28(bit_invertor_1_output29), .row29(bit_invertor_1_output30),
    .row30(bit_invertor_1_output31), .row31(bit_invertor_1_output32));
  Register #(.width(32)) register_8 (
    .D(bit_invertor_1_changed_string), .Q(inverted_row), .clk(not_25_out));  // open: en, clr
  assign controlled_buffer_18_out = decoder_11_out0 ? bus : 8'bz;  // Controlled_Buffer controlled_buffer_18
  assign controlled_buffer_18_out = recieve_row ? cpuRow[23:16] : 8'bz;  // Controlled_Buffer controlled_buffer_19
  or or_3 (or_3_out, recieve_row_slow, decoder_11_out0);
  // Probe on inverted_row
  Decoder #(.disabled(0)) decoder_11 (.out0(decoder_11_out0), .out1(decoder_11_out1), .sel(in_out), .en(and_12_out));
  assign bus = decoder_11_out1 ? register_9_q : 8'bz;  // Controlled_Buffer controlled_buffer_20
  Register register_9 (.D(controlled_buffer_18_out), .Q(register_9_q), .clk(or_3_out));  // open: en, clr
  not not_26 (not_26_out, not_26_out);
  not not_27 (not_27_out, not_27_out);
  Comparator comparator_11 (.a(IOaddr), .b(8'hf8), .eq(comparator_11_eq));  // open: gt, lt
  assign cpuRow[23:16] = send_row ? register_9_q : 8'bz;  // Controlled_Buffer controlled_buffer_21
  and and_12 (and_12_out, comparator_11_eq, IOsel);
  assign controlled_buffer_22_out = recieve_row ? cpuRow[31:24] : 8'bz;  // Controlled_Buffer controlled_buffer_22
  assign bus = decoder_12_out1 ? env_sum : 8'bz;  // Controlled_Buffer controlled_buffer_23
  Register register_10 (.D(bus), .Q(register_10_q), .clk(not_28_out));  // open: en, clr
  not not_28 (not_28_out, not_29_out);
  assign controlled_buffer_22_out = decoder_14_out0 ? bus : 8'bz;  // Controlled_Buffer controlled_buffer_24
  Register register_11 (.D(controlled_buffer_22_out), .Q(register_11_q), .clk(or_4_out));  // open: en, clr
  or or_4 (or_4_out, recieve_row_slow, decoder_14_out0);
  Comparator comparator_12 (.a(IOaddr), .b(8'hfb), .eq(comparator_12_eq));  // open: gt, lt
  Decoder #(.disabled(0)) decoder_12 (.out1(decoder_12_out1), .sel(in_out), .en(and_13_out));  // open: out0
  Decoder #(.disabled(0)) decoder_13 (.out0(decoder_13_out0), .sel(in_out), .en(and_14_out));  // open: out1
  not not_29 (not_29_out, decoder_13_out0);
  Decoder #(.disabled(0)) decoder_14 (.out0(decoder_14_out0), .out1(decoder_14_out1), .sel(in_out), .en(and_15_out));
  assign bus = decoder_14_out1 ? register_11_q : 8'bz;  // Controlled_Buffer controlled_buffer_25
  and and_13 (and_13_out, comparator_12_eq, IOsel);
  Comparator comparator_13 (.a(IOaddr), .b({8{1'b1}}), .eq(comparator_13_eq));  // open: gt, lt
  and and_14 (and_14_out, comparator_13_eq, IOsel);
  Comparator comparator_14 (.a(IOaddr), .b(8'hf9), .eq(comparator_14_eq));  // open: gt, lt
  assign cpuRow[31:24] = send_row ? register_11_q : 8'bz;  // Controlled_Buffer controlled_buffer_26
  not not_30 (not_30_out, not_30_out);
  and and_15 (and_15_out, comparator_14_eq, IOsel);
  not not_31 (not_31_out, not_31_out);
  Comparator comparator_15 (.a(8'h40), .b(register_10_q), .eq(comparator_15_eq));  // open: gt, lt
  Comparator comparator_16 (.a(8'h41), .b(register_10_q), .eq(comparator_16_eq));  // open: gt, lt
  Comparator comparator_17 (.a(8'h42), .b(register_10_q), .eq(comparator_17_eq));  // open: gt, lt
  assign bus = decoder_15_out1 ? {{7{1'b0}}, is_row_null} : 8'bz;  // Controlled_Buffer controlled_buffer_27
  LED led_3 (.in(comparator_15_eq));
  LED led_4 (.in(comparator_16_eq));
  LED led_5 (.in(comparator_17_eq));
  Decoder #(.disabled(0)) decoder_15 (.out1(decoder_15_out1), .sel(in_out), .en(and_16_out));  // open: out0
  Comparator comparator_18 (.a(IOaddr), .b(8'hfc), .eq(comparator_18_eq));  // open: gt, lt
  and and_16 (and_16_out, comparator_18_eq, IOsel);
  not not_32 (not_32_out, not_32_out);
  assign bus = decoder_16_out1 ? {{7{1'b0}}, is_null_byte} : 8'bz;  // Controlled_Buffer controlled_buffer_28
  Comparator comparator_19 (.a(IOaddr), .b(8'hfd), .eq(comparator_19_eq));  // open: gt, lt
  Decoder #(.disabled(0)) decoder_16 (.out1(decoder_16_out1), .sel(in_out), .en(and_17_out));  // open: out0
  and and_17 (and_17_out, comparator_19_eq, IOsel);
  // Probe on cdm_8_mark5_2_p1
  // Probe on cdm_8_mark5_2_p5
  // Probe on cdm_8_mark5_2_p2
  // Probe on cdm_8_mark5_2_p4
  Clock clock_2 (.out(clock));
  not not_33 (not_33_out, comparator_20_lt);
  and and_18 (IOsel_1, not_33_out, clock, data_1);
  not not_34 (not_34_out, not_34_out);
  not not_35 (not_35_out, not_35_out);
  not not_36 (not_36_out, not_36_out);
  // Probe on cdm_8_mark5_2_p6
  // Probe on cdm_8_mark5_2_p7
  // Probe on cdm_8_mark5_2_p8
  // CdM_8_mark5 cdm_8_mark5_2: pin names not known; wires that end beside it: cdm_8_mark5_2_p1, cdm_8_mark5_2_p2, clock, cdm_8_mark5_2_p4, cdm_8_mark5_2_p5, cdm_8_mark5_2_p6, cdm_8_mark5_2_p7, cdm_8_mark5_2_p8, cdm_8_mark5_2_p9, mem_1, in_out_1, IOaddr_1, cdm_8_mark5_2_p13, cdm_8_mark5_2_p14
  not not_37 (send_row_slow, not_38_out);
  not not_38 (not_38_out, send_row);
  not not_39 (not_39_out, recieve_row);
  not not_40 (recieve_row_slow, not_39_out);
  Decoder #(.disabled(0)) decoder_17 (.out0(code_1), .out1(data_1), .sel(cdm_8_mark5_2_p9), .en(mem_1));
  assign bus_1 = not_41_out ? cdm_8_mark5_2_p13 : 8'bz;  // Controlled_Buffer controlled_buffer_29
  not not_41 (not_41_out, in_out_1);
  assign cdm_8_mark5_2_p14 = in_out_1 ? bus_1 : 8'bz;  // Controlled_Buffer controlled_buffer_30
  and and_19 (RAM_1, comparator_20_lt, data_1);
  // Probe on IOaddr_1
  assign bus_1 = recieve_row ? {8{1'b0}} : 8'bz;  // Controlled_Buffer controlled_buffer_31
  assign controlled_buffer_32_out = decoder_19_out0 ? bus_1 : 8'bz;  // Controlled_Buffer controlled_buffer_32
  Register register_12 (.D(controlled_buffer_32_out), .Q({register_12_q, cpuY_1}), .clk(not_42_out));  // open: en, clr
  not not_42 (not_42_out, not_43_out);
  not not_43 (not_43_out, decoder_19_out0);
  assign bus_1 = decoder_20_out1 ? IO_game_mode : 8'bz;  // Controlled_Buffer controlled_buffer_33
  Comparator #(.mode("unsigned")) comparator_20 (.a(IOaddr_1), .b(8'hf0), .lt(comparator_20_lt));  // open: gt, eq
  Decoder #(.disabled(0)) decoder_18 (.out0(send_row), .out1(recieve_row), .sel(in_out_1), .en(and_20_out));
  Decoder #(.disabled(0)) decoder_19 (.out0(decoder_19_out0), .sel(in_out_1), .en(and_21_out));  // open: out1
  Decoder #(.disabled(0)) decoder_20 (.out1(decoder_20_out1), .sel(in_out_1), .en(and_22_out));  // open: out0
  ROM rom_2 (.addr(IOaddr_1), .data(bus_1), .sel(code_1));
  RAM ram_2 (.addr(IOaddr_1), .data(bus_1), .sel(RAM_1), .clk(clock), .ld(in_out_1));  // open: clr
  Comparator comparator_21 (.a(IOaddr_1), .b(8'hf5), .eq(comparator_21_eq));  // open: gt, lt
  and and_20 (and_20_out, comparator_21_eq, IOsel_1);
  Comparator comparator_22 (.a(IOaddr_1), .b(8'hf3), .eq(comparator_22_eq));  // open: gt, lt
  and and_21 (and_21_out, comparator_22_eq, IOsel_1);
  Comparator comparator_23 (.a(IOaddr_1), .b(8'hf0), .eq(comparator_23_eq));  // open: gt, lt
  and and_22 (and_22_out, comparator_23_eq, IOsel_1);
  // Probe on bus_1
  not not_44 (not_44_out, not_44_out);
  not not_45 (not_45_out, not_45_out);
  assign controlled_buffer_34_out = decoder_21_out0 ? bus_1 : 8'bz;  // Controlled_Buffer controlled_buffer_34
  assign controlled_buffer_34_out = recieve_row ? cpuRow[7:0] : 8'bz;  // Controlled_Buffer controlled_buffer_35
  or or_5 (or_5_out, recieve_row_slow, decoder_21_out0);
  assign controlled_buffer_36_out = decoder_22_out0 ? bus_1 : 8'bz;  // Controlled_Buffer controlled_buffer_36
  not not_46 (not_46_out, not_47_out);
  Decoder #(.disabled(0)) decoder_21 (.out0(decoder_21_out0), .out1(decoder_21_out1), .sel(in_out_1), .en(and_23_out));
  assign bus_1 = decoder_21_out1 ? register_13_q : 8'bz;  // Controlled_Buffer controlled_buffer_37
  Register register_13 (.D(controlled_buffer_34_out), .Q(register_13_q), .clk(or_5_out));  // open: en, clr
  Decoder #(.disabled(0)) decoder_22 (.out0(decoder_22_out0), .sel(in_out_1), .en(and_24_out));  // open: out1
  Register register_14 (.D(controlled_buffer_36_out), .Q({register_14_q, cpuX_1}), .clk(not_46_out));  // open: en, clr
  not not_47 (not_47_out, decoder_22_out0);
  assign bus_1 = decoder_23_out1 ? IO_birth_conditions : 8'bz;  // Controlled_Buffer controlled_buffer_38
  Comparator comparator_24 (.a(IOaddr_1), .b(8'hf6), .eq(comparator_24_eq));  // open: gt, lt
  assign cpuRow[7:0] = send_row ? register_13_q : 8'bz;  // Controlled_Buffer controlled_buffer_39
  Comparator comparator_25 (.a(IOaddr_1), .b(8'hf4), .eq(comparator_25_eq));  // open: gt, lt
  Comparator comparator_26 (.a(IOaddr_1), .b(8'hf1), .eq(comparator_26_eq));  // open: gt, lt
  Decoder #(.disabled(0)) decoder_23 (.out1(decoder_23_out1), .sel(in_out_1), .en(and_25_out));  // open: out0
  and and_23 (and_23_out, comparator_24_eq, IOsel_1);
  and and_24 (and_24_out, comparator_25_eq, IOsel_1);
  and and_25 (and_25_out, comparator_26_eq, IOsel_1);
  assign controlled_buffer_40_out = recieve_row ? cpuRow[15:8] : 8'bz;  // Controlled_Buffer controlled_buffer_40
  not not_48 (not_48_out, not_48_out);
  not not_49 (not_49_out, not_49_out);
  assign controlled_buffer_40_out = decoder_24_out0 ? bus_1 : 8'bz;  // Controlled_Buffer controlled_buffer_41
  Register register_15 (.D(controlled_buffer_40_out), .Q(register_15_q), .clk(or_6_out));  // open: en, clr
  or or_6 (or_6_out, recieve_row_slow, decoder_24_out0);
  Decoder #(.disabled(0)) decoder_24 (.out0(decoder_24_out0), .out1(decoder_24_out1), .sel(in_out_1), .en(and_26_out));
  assign bus_1 = decoder_24_out1 ? register_15_q : 8'bz;  // Controlled_Buffer controlled_buffer_42
  Comparator comparator_27 (.a(IOaddr_1), .b(8'hf7), .eq(comparator_27_eq));  // open: gt, lt
  assign cpuRow[15:8] = send_row ? register_15_q : 8'bz;  // Controlled_Buffer controlled_buffer_43
  assign bus_1 = decoder_25_out1 ? {{7{1'b0}}, selected_bit_1} : 8'bz;  // Controlled_Buffer controlled_buffer_44
  assign bus_1 = decoder_26_out1 ? IO_death_conditions : 8'bz;  // Controlled_Buffer controlled_buffer_45
  and and_26 (and_26_out, comparator_27_eq, IOsel_1);
  Decoder #(.disabled(0)) decoder_25 (.out1(decoder_25_out1), .sel(in_out_1), .en(and_27_out));  // open: out0
  Decoder #(.disabled(0)) decoder_26 (.out1(decoder_26_out1), .sel(in_out_1), .en(and_28_out));  // open: out0
  assign controlled_buffer_46_out = recieve_row ? cpuRow[23:16] : 8'bz;  // Controlled_Buffer controlled_buffer_46
  Comparator comparator_28 (.a(IOaddr_1), .b(8'hfa), .eq(comparator_28_eq));  // open: gt, lt
  and and_27 (and_27_out, comparator_28_eq, IOsel_1);
  Comparator comparator_29 (.a(IOaddr_1), .b(8'hf2), .eq(comparator_29_eq));  // open: gt, lt
  and and_28 (and_28_out, comparator_29_eq, IOsel_1);
  assign controlled_buffer_46_out = decoder_27_out0 ? bus_1 : 8'bz;  // Controlled_Buffer controlled_buffer_47
  assign bus_1 = decoder_27_out1 ? register_16_q : 8'bz;  // Controlled_Buffer controlled_buffer_48
  Register register_16 (.D(controlled_buffer_46_out), .Q(register_16_q), .clk(or_7_out));  // open: en, clr
  or or_7 (or_7_out, recieve_row_slow, decoder_27_out0);
  not not_50 (not_50_out, not_50_out);
  Decoder #(.disabled(0)) decoder_27 (.out0(decoder_27_out0), .out1(decoder_27_out1), .sel(in_out_1), .en(and_29_out));
  assign cpuRow[23:16] = send_row ? register_16_q : 8'bz;  // Controlled_Buffer controlled_buffer_49
  not not_51 (not_51_out, not_51_out);
  Comparator comparator_30 (.a(IOaddr_1), .b(8'hf8), .eq(comparator_30_eq));  // open: gt, lt
  and and_29 (and_29_out, comparator_30_eq, IOsel_1);
  assign controlled_buffer_50_out = recieve_row ? cpuRow[31:24] : 8'bz;  // Controlled_Buffer controlled_buffer_50
  Decoder #(.disabled(0)) decoder_28 (.out1(decoder_28_out1), .sel(in_out_1), .en(and_30_out));  // open: out0
  assign bus_1 = decoder_28_out1 ? env_sum_1 : 8'bz;  // Controlled_Buffer controlled_buffer_51
  Register register_17 (.D(bus), .Q(register_17_q), .clk(not_53_out));  // open: en, clr
  not not_52 (not_52_out, decoder_29_out0);
  not not_53 (not_53_out, not_52_out);
  assign bus_1 = decoder_30_out1 ? register_18_q : 8'bz;  // Controlled_Buffer controlled_buffer_52
  assign controlled_buffer_50_out = decoder_30_out0 ? bus_1 : 8'bz;  // Controlled_Buffer controlled_buffer_53
  Register register_18 (.D(controlled_buffer_50_out), .Q(register_18_q), .clk(or_8_out));  // open: en, clr
  or or_8 (or_8_out, recieve_row_slow, decoder_30_out0);
  Comparator comparator_31 (.a(IOaddr_1), .b(8'hfb), .eq(comparator_31_eq));  // open: gt, lt
  and and_30 (and_30_out, comparator_31_eq, IOsel_1);
  Decoder #(.disabled(0)) decoder_29 (.out0(decoder_29_out0), .sel(in_out), .en(and_31_out));  // open: out1
  Decoder #(.disabled(0)) decoder_30 (.out0(decoder_30_out0), .out1(decoder_30_out1), .sel(in_out_1), .en(and_32_out));
  assign cpuRow[31:24] = send_row ? register_18_q : 8'bz;  // Controlled_Buffer controlled_buffer_54
  Comparator comparator_32 (.a(IOaddr), .b({8{1'b1}}), .eq(comparator_32_eq));  // open: gt, lt
  and and_31 (and_31_out, comparator_32_eq, IOsel);
  Comparator comparator_33 (.a(IOaddr_1), .b(8'hf9), .eq(comparator_33_eq));  // open: gt, lt
  and and_32 (and_32_out, comparator_33_eq, IOsel_1);
  not not_54 (not_54_out, not_54_out);
  not not_55 (not_55_out, not_55_out);
  Comparator comparator_34 (.a(8'h40), .b(register_17_q), .eq(comparator_34_eq));  // open: gt, lt
  Comparator comparator_35 (.a(8'h41), .b(register_17_q), .eq(comparator_35_eq));  // open: gt, lt
  Comparator comparator_36 (.a(8'h42), .b(register_17_q), .eq(comparator_36_eq));  // open: gt, lt
  assign bus_1 = decoder_31_out1 ? {{7{1'b0}}, is_row_null_1} : 8'bz;  // Controlled_Buffer controlled_buffer_55
  LED led_6 (.in(comparator_34_eq));
  LED led_7 (.in(comparator_35_eq));
  LED led_8 (.in(comparator_36_eq));
  Decoder #(.disabled(0)) decoder_31 (.out1(decoder_31_out1), .sel(in_out_1), .en(and_33_out));  // open: out0
  Comparator comparator_37 (.a(IOaddr_1), .b(8'hfc), .eq(comparator_37_eq));  // open: gt, lt
  and and_33 (and_33_out, comparator_37_eq, IOsel_1);
  not not_56 (not_56_out, not_56_out);
  Decoder #(.disabled(0)) decoder_32 (.out1(decoder_32_out1), .sel(in_out_1), .en(and_34_out));  // open: out0
  assign bus_1 = decoder_32_out1 ? {{7{1'b0}}, is_null_byte_1} : 8'bz;  // Controlled_Buffer controlled_buffer_56
  Comparator comparator_38 (.a(IOaddr_1), .b(8'hfd), .eq(comparator_38_eq));  // open: gt, lt
  and and_34 (and_34_out, comparator_38_eq, IOsel_1);

  // Other names for the same wires on the sheet: IOdata[7:0] = bus; IOdata_1[7:0] = bus_1; playing = IO_game_mode[0];
  //   rd_wr = in_out; rd_wr_1 = in_out_1

  // Notes on the sheet:
  //   Keyboard
  //   ROW READ / WRITE
  //   (read only thus CdM -> buffer)
  //   PROCESSED CELL
  //   READ ONLY INPUTS
  //   (immutable game state)
  //   Structure of I/O bus
  //   Cell 0xf3 (Y - row)
  //   Cell 0xf5 (row data direction)
  //   Cell 0xf0 (state)
  //   Harvard Architecture
  //   Minimal IO cell address
  //   contents of rom_1 (hex, n*v repeats v):
  //   ee 36 d2 8 d1 0 18 a e0 11 88 b3 95 1d 8a ee 7 4 d7 d3 8 f e0 21 d2 1 42 a6 8d 98 8b ee 15 d7 5 e1
  //   29 d2 60 ee 2b d2 68 88 12 ba a e0 35 8d d0 1 41 d7 cd 50 d0 ff d1 40 a1 d1 f0 b4 0 e0 3f d1 50 a4
  //   d1 f1 b4 d1 60 d6 13 d1 f2 b4 d1 68 d6 13 d0 ff d1 42 a1 d3 1f d2 ef c3 d0 f3 a3 d3 fc bf f e1 a4 d1
  //   1f d3 4 c3 c2 d2 0 d0 f4 a1 d0 fd b0 0 e1 97 d3 8 c1 d0 f4 a1 d0 fb b0 0 e0 8f d1 fa b5 c2 d6 22 c6
  //   96 16 ee 90 96 c5 89 8b e1 7a ee 9a d0 f8 11 8 c6 a8 8a c7 8b e1 6b ee a8 4*8a c7 d0 fe 13 e5 5d d4
  //   d0 ff d1 41 a1 d0 ef d3 1f d1 f3 a7 d1 f9 b2 a6 88 89 d2 f6 76 ea bd d1 f5 a5 d1 fe 17 e5 b8 ee 54
  //   d4
  //   Cells 0xf6-0xf9
  //   (little endtian row's bytes)
  //   Cell 0xf4 (X - bit)
  //   Cell 0xf1 (birth conditions)
  //   Cell 0xfa (bit value)
  //   Cell 0xf2 (survival conditions)
  //   DEV I/O REGS.
  //   Cell 0xfb (env. sum)
  //   Cell 0xff (CPU status)
  //   Cell 0xfc (is null rows env.)
  //   waiting for start
  //   reading field
  //   processing field
  //   Cell 0xfd (is null byte env.)
  //   ROW READ / WRITE
  //   (read only thus CdM -> buffer)
  //   PROCESSED CELL
  //   READ ONLY INPUTS
  //   (immutable game state)
  //   Structure of I/O bus
  //   Cell 0xf5 (row data direction)
  //   Cell 0xf3 (Y - row)
  //   Cell 0xf0 (state)
  //   Harvard Architecture
  //   Minimal IO cell address
  //   contents of rom_2 (hex, n*v repeats v):
  //   ee 36 d2 8 d1 0 18 a e0 11 88 b3 95 1d 8a ee 7 4 d7 d3 8 f e0 21 d2 1 42 a6 8d 98 8b ee 15 d7 5 e1
  //   29 d2 60 ee 2b d2 68 88 12 ba a e0 35 8d d0 1 41 d7 cd 50 d0 ff d1 40 a1 d1 f0 b4 0 e0 3f d1 50 a4
  //   d1 f1 b4 d1 60 d6 13 d1 f2 b4 d1 68 d6 13 d0 ff d1 42 a1 d3 1e d2 ef c3 d0 f3 a3 d3 fc bf f e1 a4 d1
  //   1f d3 4 c3 c2 d2 0 d0 f4 a1 d0 fd b0 0 e1 97 d3 8 c1 d0 f4 a1 d0 fb b0 0 e0 8f d1 fa b5 c2 d6 22 c6
  //   96 16 ee 90 96 c5 89 8b e1 7a ee 9a d0 f8 11 8 c6 a8 8a c7 8b e1 6b ee a8 4*8a c7 d0 fe 13 e5 5d d4
  //   d0 ff d1 41 a1 d0 ef d3 1e d1 f3 a7 d1 f9 b2 a6 88 89 d2 f6 76 ea bd d1 f5 a5 d1 fe 17 e5 b8 ee 54
  //   d4
  //   Cells 0xf6-0xf9
  //   (little endtian row's bytes)
  //   Cell 0xf4 (X - bit)
  //   Cell 0xf1 (birth conditions)
  //   Cell 0xfa (bit value)
  //   Cell 0xf2 (survival conditions)
  //   DEV I/O REGS.
  //   Cell 0xfb (env. sum)
  //   Cell 0xff (CPU status)
  //   Cell 0xfc (is null rows env.)
  //   waiting for start
  //   reading field
  //   processing field
  //   Cell 0xfd (is null byte env.)
endmodule

module env_constructor (
  input  [31:0] Row_0,
  input  [31:0] Row_1,
  input  [31:0] Row_2,
  input  [31:0] Row_3,
  input  [31:0] Row_4,
  input  [31:0] Row_5,
  input  [31:0] Row_6,
  input  [31:0] Row_7,
  input  [31:0] Row_8,
  input  [31:0] Row_9,
  input  [31:0] Row_10,
  input  [31:0] Row_11,
  input  [31:0] Row_12,
  input  [31:0] Row_13,
  input  [31:0] Row_14,
  input  [31:0] Row_15,
  input  [31:0] Row_16,
  input  [31:0] Row_17,
  input  [31:0] Row_18,
  input  [31:0] Row_19,
  input  [31:0] Row_20,
  input  [31:0] Row_21,
  input  [31:0] Row_22,
  input  [31:0] Row_23,
  input  [31:0] Row_24,
  input  [31:0] Row_25,
  input  [31:0] Row_26,
  input  [31:0] Row_27,
  input  [31:0] Row_28,
  input  [31:0] Row_29,
  input  [31:0] Row_30,
  input  [31:0] Row_31,
  input  [4:0] Y__row_index,
  input  [4:0] X__bit_index,
  output Is_row_env__null,
  output Is_byte_env__null,
  output [7:0] Sum,
  output Bit
);

  wire nor_1_out, nor_2_out, nor_3_out, nor_4_out, nor_5_out, nor_6_out, nor_7_out, nor_8_out, nor_9_out;
  wire [4:0] adder_1_out, adder_2_out, adder_3_out;
  wire [7:0] adder_4_out, adder_5_out, adder_6_out, adder_7_out, adder_8_out, adder_9_out, adder_10_out;
  wire [31:0] multiplexer_1_out, multiplexer_2_out, multiplexer_3_out, shifter_1_out, shifter_2_out,
       shifter_3_out;

  Adder #(.width(5)) adder_1 (.a({5{1'b1}}), .b(Y__row_index), .out(adder_1_out));  // open: cin, cout
  Adder #(.width(5)) adder_2 (.a(Y__row_index), .b(5'b00001), .out(adder_2_out));  // open: cin, cout
  Multiplexer #(.select(5), .width(32), .enable("false")) multiplexer_1 (
    .in0(Row_0), .in1(Row_1), .in2(Row_2), .in3(Row_3), .in4(Row_4), .in5(Row_5), .in6(Row_6), .in7(Row_7),
    .in8(Row_8), .in9(Row_9), .in10(Row_10), .in11(Row_11), .in12(Row_12), .in13(Row_13), .in14(Row_14),
    .in15(Row_15), .in16(Row_16), .in17(Row_17), .in18(Row_18), .in19(Row_19), .in20(Row_20), .in21(Row_21),
    .in22(Row_22), .in23(Row_23), .in24(Row_24), .in25(Row_25), .in26(Row_26), .in27(Row_27), .in28(Row_28),
    .in29(Row_29), .in30(Row_30), .in31(Row_31), .out(multiplexer_1_out), .sel(adder_1_out));
  Multiplexer #(.select(5), .width(32), .enable("false")) multiplexer_2 (
    .in0(Row_0), .in1(Row_1), .in2(Row_2), .in3(Row_3), .in4(Row_4), .in5(Row_5), .in6(Row_6), .in7(Row_7),
    .in8(Row_8), .in9(Row_9), .in10(Row_10), .in11(Row_11), .in12(Row_12), .in13(Row_13), .in14(Row_14),
    .in15(Row_15), .in16(Row_16), .in17(Row_17), .in18(Row_18), .in19(Row_19), .in20(Row_20), .in21(Row_21),
    .in22(Row_22), .in23(Row_23), .in24(Row_24), .in25(Row_25), .in26(Row_26), .in27(Row_27), .in28(Row_28),
    .in29(Row_29), .in30(Row_30), .in31(Row_31), .out(multiplexer_2_out), .sel(Y__row_index));
  Multiplexer #(.select(5), .width(32), .enable("false")) multiplexer_3 (
    .in0(Row_0), .in1(Row_1), .in2(Row_2), .in3(Row_3), .in4(Row_4), .in5(Row_5), .in6(Row_6), .in7(Row_7),
    .in8(Row_8), .in9(Row_9), .in10(Row_10), .in11(Row_11), .in12(Row_12), .in13(Row_13), .in14(Row_14),
    .in15(Row_15), .in16(Row_16), .in17(Row_17), .in18(Row_18), .in19(Row_19), .in20(Row_20), .in21(Row_21),
    .in22(Row_22), .in23(Row_23), .in24(Row_24), .in25(Row_25), .in26(Row_26), .in27(Row_27), .in28(Row_28),
    .in29(Row_29), .in30(Row_30), .in31(Row_31), .out(multiplexer_3_out), .sel(adder_2_out));
  // Probe on adder_3_out
  Adder #(.width(5)) adder_3 (.a({5{1'b1}}), .b(X__bit_index), .out(adder_3_out));  // open: cin, cout
  Adder adder_4 (.a({8{1'b0}}), .b({8{1'b0}}), .out(adder_4_out), .cin(shifter_3_out[2]));  // open: cout
  Shifter #(.width(32), .shift("rr")) shifter_1 (.in(multiplexer_1_out), .\dist (adder_3_out), .out(shifter_1_out));
  Shifter #(.width(32), .shift("rr")) shifter_2 (
    .in(multiplexer_2_out), .\dist (adder_3_out), .out({shifter_2_out[31:2], Bit, shifter_2_out[0]}));
  Shifter #(.width(32), .shift("rr")) shifter_3 (.in(multiplexer_3_out), .\dist (adder_3_out), .out(shifter_3_out));
  Adder adder_5 (.a({8{1'b0}}), .b(adder_4_out), .out(adder_5_out), .cin(shifter_3_out[1]));  // open: cout
  Adder adder_6 (.a(adder_5_out), .b({8{1'b0}}), .out(adder_6_out), .cin(shifter_3_out[0]));  // open: cout
  Adder adder_7 (.a({8{1'b0}}), .b(adder_6_out), .out(adder_7_out), .cin(shifter_2_out[2]));  // open: cout
  Adder adder_8 (.a(adder_7_out), .b({8{1'b0}}), .out(adder_8_out), .cin(shifter_2_out[0]));  // open: cout
  Adder adder_9 (.a({8{1'b0}}), .b(adder_8_out), .out(adder_9_out), .cin(shifter_1_out[2]));  // open: cout
  nor nor_1 (nor_1_out, shifter_1_out[31], shifter_1_out[30], shifter_1_out[29], shifter_1_out[28], shifter_1_out[27], shifter_1_out[26], shifter_1_out[25], shifter_1_out[24], shifter_1_out[23], shifter_1_out[22], shifter_1_out[21], shifter_1_out[20], shifter_1_out[19], shifter_1_out[18], shifter_1_out[17], shifter_1_out[16], shifter_1_out[14], shifter_1_out[13], shifter_1_out[12], shifter_1_out[11], shifter_1_out[10], shifter_1_out[9], shifter_1_out[8], shifter_1_out[7], shifter_1_out[6], shifter_1_out[5], shifter_1_out[4], shifter_1_out[3], shifter_1_out[2], shifter_1_out[1], shifter_1_out[0], shifter_1_out[15]);
  nor nor_2 (nor_2_out, shifter_2_out[31], shifter_2_out[30], shifter_2_out[29], shifter_2_out[28], shifter_2_out[27], shifter_2_out[26], shifter_2_out[25], shifter_2_out[24], shifter_2_out[23], shifter_2_out[22], shifter_2_out[21], shifter_2_out[20], shifter_2_out[19], shifter_2_out[18], shifter_2_out[17], shifter_2_out[16], shifter_2_out[14], shifter_2_out[13], shifter_2_out[12], shifter_2_out[11], shifter_2_out[10], shifter_2_out[9], shifter_2_out[8], shifter_2_out[7], shifter_2_out[6], shifter_2_out[5], shifter_2_out[4], shifter_2_out[3], shifter_2_out[2], Bit, shifter_2_out[0], shifter_2_out[15]);
  nor nor_3 (nor_3_out, shifter_3_out[31], shifter_3_out[30], shifter_3_out[29], shifter_3_out[28], shifter_3_out[27], shifter_3_out[26], shifter_3_out[25], shifter_3_out[24], shifter_3_out[23], shifter_3_out[22], shifter_3_out[21], shifter_3_out[20], shifter_3_out[19], shifter_3_out[18], shifter_3_out[17], shifter_3_out[16], shifter_3_out[14], shifter_3_out[13], shifter_3_out[12], shifter_3_out[11], shifter_3_out[10], shifter_3_out[9], shifter_3_out[8], shifter_3_out[7], shifter_3_out[6], shifter_3_out[5], shifter_3_out[4], shifter_3_out[3], shifter_3_out[2], shifter_3_out[1], shifter_3_out[0], shifter_3_out[15]);
  Adder adder_10 (.a(adder_9_out), .b({8{1'b0}}), .out(adder_10_out), .cin(shifter_1_out[1]));  // open: cout
  Adder adder_11 (.a({8{1'b0}}), .b(adder_10_out), .out(Sum), .cin(shifter_1_out[0]));  // open: cout
  and and_1 (Is_row_env__null, nor_1_out, nor_2_out, nor_3_out);
  nor nor_4 (nor_4_out, shifter_1_out[31], shifter_1_out[30], shifter_1_out[29], shifter_1_out[28], shifter_1_out[27], shifter_1_out[26], shifter_1_out[25]);
  nor nor_5 (nor_5_out, shifter_2_out[31], shifter_2_out[30], shifter_2_out[29], shifter_2_out[28], shifter_2_out[27], shifter_2_out[26], shifter_2_out[25]);
  nor nor_6 (nor_6_out, shifter_3_out[31], shifter_3_out[30], shifter_3_out[29], shifter_3_out[28], shifter_3_out[27], shifter_3_out[26], shifter_3_out[25]);
  nor nor_7 (nor_7_out, shifter_1_out[2], shifter_1_out[1], shifter_1_out[0]);
  nor nor_8 (nor_8_out, shifter_2_out[2], Bit, shifter_2_out[0]);
  nor nor_9 (nor_9_out, shifter_3_out[2], shifter_3_out[1], shifter_3_out[0]);
  and and_2 (Is_byte_env__null, nor_7_out, nor_4_out, nor_8_out, nor_5_out, nor_9_out, nor_6_out);

  // Other names for the same wires on the sheet: row0[31:0] = Row_0; row1[31:0] = Row_1; row2[31:0] = Row_2;
  //   row3[31:0] = Row_3; row4[31:0] = Row_4; row5[31:0] = Row_5; row6[31:0] = Row_6; row7[31:0] = Row_7;
  //   row8[31:0] = Row_8; row9[31:0] = Row_9; row10[31:0] = Row_10; row11[31:0] = Row_11; row12[31:0] = Row_12;
  //   row13[31:0] = Row_13; row14[31:0] = Row_14; row15[31:0] = Row_15; row16[31:0] = Row_16; row17[31:0] = Row_17;
  //   row18[31:0] = Row_18; row19[31:0] = Row_19; row20[31:0] = Row_20; row21[31:0] = Row_21; row22[31:0] = Row_22;
  //   row23[31:0] = Row_23; row24[31:0] = Row_24; row25[31:0] = Row_25; row26[31:0] = Row_26; row27[31:0] = Row_27;
  //   row28[31:0] = Row_28; row29[31:0] = Row_29; row30[31:0] = Row_30; row31[31:0] = Row_31
endmodule
